# Fritzing sketch 3PawnGame_Fritz (saved by Fritzing 0.9.9b)
breadboards: 2

parts:
  Argon1 = Particle Argon
  R1 = Resistor [tolerance=±5% power=0.25 resistance=10k package=THT]
  R2 = Resistor [tolerance=±5% power=0.25 resistance=10k package=THT]
  R3 = Resistor [tolerance=±5% power=0.25 resistance=10k package=THT]

nets:
  N1: Argon1.A1, Argon1.A2, Argon1.A3, Argon1.D2, Argon1.D3, Argon1.D4, R1.Pin_1, R2.Pin_0, R3.Pin_1

custom parts:
  Particle Argon: The Argon is a powerful Wi-Fi enabled development board that can act as either a standalone Wi-Fi endpoint or Wi-Fi enabled gateway for Particle Mesh networks. It is based on the Nordic nRF52840 and has built-in battery charging circuitry so it’s easy to connect a Li-Po and deploy your local network in minutes. The Argon is great for connecting existing projects to the Particle Device Cloud or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
